# Fritzing sketch elie final projemcts (saved by Fritzing 0.9.3b)
circuit board: 8.46667cm x 5.64444cm
breadboards: 1

parts:
  Part1 = Arduino Uno (Rev3) - ICSP
  Part2 = Soil Moisture Sensor
  LED1 = LEDs [package=led10mm]
  J1 = Piezo Speaker

nets:
  N1: Part1.A0, Part2.SIG
  5V: Part1.5V, Part2.VCC
  GND: Part1.GND, Part2.GND, LED1.A, J1.pin1
  N2: Part1.D3_PWM, LED1.C
  N3: Part1.D4, J1.pin2

// code stored in the sketch: eliees final projects.ino
void setup()
{
  Serial.begin(9600);
  pinMode(3,OUTPUT);
   pinMode(4,OUTPUT);
 }

void loop() 
{
int level;
level=analogRead(A0);
Serial.println("analogvalue:");
Serial.println(level);
digitalWrite(3,LOW);
digitalWrite(4,LOW);
if(level<1000){
  digitalWrite(3,HIGH);
digitalWrite(4,HIGH);
}
}

// code stored in the sketch: Untitled2.ino
int moisture_sensor=A0; 
int led=3; 
int buzzer=4; 
  
void setup () 
{ 
  Serial.begin(9600); 
  pinMode(moisture_sensor,INPUT); 
  pinMode (3, OUTPUT); 
   pinMode (4, OUTPUT); 
 } 
  
void loop () 
{ 
int level; 
level=analogRead(A0); 
Serial.println("analogvalue:"); 
Serial.println(level); 
DigitalWrite (3, LOW); 
DigitalWrite (4, LOW); 
if(level<1000) { 
  digitalWrite (3, HIGH); 
digitalWrite (4, HIGH); 
} 
}
